// Logisim project seq_circuit.circ as structural Verilog: 1 circuit, main circuit main
module main (
  input  x,
  input  y,
  output s
);

  wire and_1_out, and_2_out, clock_1_out, or_1_out, xor_1_out;

  xor xor_1 (xor_1_out, x, y);
  and and_1 (and_1_out, x, y);
  Clock clock_1 (.out(clock_1_out));
  D_Flip_Flop d_ff_1 (.clk(clock_1_out), .D(or_1_out), .Q(and_1_out));  // open: Qn, preset, en, reset
  and and_2 (and_2_out, xor_1_out, and_1_out);
  xor xor_2 (s, xor_1_out, and_1_out);
  or or_1 (or_1_out, and_2_out, and_1_out);

  // Notes on the sheet:
  //   Clock
endmodule
